# Fritzing sketch incubator (saved by Fritzing 0.9.3b)

parts:
  U1 = Voltage Regulator - 5V [package="TO220 [THT]"]
  RHT1 = Humidity and Temperature Sensor RHT03
  J1 = Basic Servo
  Bauteil2 = Arduino Uno (Rev3)
  R1 = Resistor [tolerance=±5% resistance=1 package=THT]
  Q1 = Basic FET N-Channel [package="DPak [SMD]"]
  Bauteil3 = LCD Keypad Shield
  J2 = Piezo Speaker

nets:
  GND: U1.GND, RHT1.GND_2, J1.gnd, Bauteil2.GND, Q1.drain, Bauteil3.GND
  N1: U1.output_voltage, J1.vcc
  VCC: RHT1.Vcc, Bauteil2.5V, Bauteil3.+5V
  N2: RHT1.Data-signal, Bauteil2.D3_PWM
  N3: J1.pulse, Bauteil2.D11_PWM/MOSI
  N4: Bauteil2.A1, Q1.Gate
  N5: Bauteil2.A2, J2.pin2
  N6: R1.Pin_1, Q1.source

notes:
  12V input soldered to power plug
  Kathal wire heating resistor
  5V regulator to power fan and servo
  12V running slowly @ 5V
  servo to open/close air vent
  DHT22 T/H probe
  MOSFET as switch for heating
  to 12V power supply
  alarm buzzer

custom parts:
  LCD Keypad Shield: It consists of a 1602 white character blue backlight LCD. The keypad consists of 5 keys — select, up, right, down and left. To save the digital IO pins, the keypad interface uses only one ADC channel. The key value is read through a 5 stage voltage divider.
